# Fritzing sketch bitirme (saved by Fritzing 0.9.2b)
breadboards: 1

parts:
  Raspberry_Pi1 = Raspberry Pi 2
  IC1 = MCP3008 8-channel 10-bit ADC [part_number=MCP3008]
  R4 = Photocell (LDR) [package=THT]
  R5 = Resistor [tolerance=±5% resistance=10k package=THT]
  U4 = 8RelayModule
  DHT1 = DHT11 Humitidy and Temperature Sensor
  R6 = Resistor [tolerance=±5% resistance=10k package=THT]  # not connected
  R7 = Resistor [tolerance=±5% resistance=10k package=THT]
  J1 = Basic Servo

nets:
  N1: Raspberry_Pi1.3v3, IC1.no_name_yet#15, IC1.no_name_yet#16, R4.pin_1
  GND: Raspberry_Pi1.GND, IC1.no_name_yet#9, IC1.no_name_yet#14, R5.Pin_0, U4.GND
  N2: Raspberry_Pi1.GPIO17, U4.IN2
  N3: Raspberry_Pi1.GPIO27, U4.IN3
  N4: Raspberry_Pi1.GPIO22, U4.IN4
  N5: Raspberry_Pi1.GPIO10, IC1.no_name_yet#11
  N6: Raspberry_Pi1.GPIO9, IC1.no_name_yet#12
  N7: Raspberry_Pi1.GPIO11, IC1.no_name_yet#13
  N8: Raspberry_Pi1.GPIO13, J1.pulse
  N9: Raspberry_Pi1.GPIO8, IC1.no_name_yet#10
  N10: Raspberry_Pi1.GPIO18, U4.IN1
  5V: Raspberry_Pi1.5V, U4.VCC
  N11: IC1.no_name_yet#1, R4.pin_0, R5.Pin_1
  N12: DHT1.VDD, R7.Pin_0
  N13: DHT1.DATA, R7.Pin_1

custom parts:
  8RelayModule: 8 relay arduino module SONGLE SRD05VDC-SL-C
  DHT11 Humitidy and Temperature Sensor: DHT11 Humidity and Temperature Sensor
